# Fritzing sketch MIDTERM PROJECT (saved by Fritzing 0.9.3b)
breadboards: 1

parts:
  Part1 = Arduino Mega 2560 (Rev3)
  R1 = Resistor [tolerance=±5% resistance=1k package=THT]
  R2 = Resistor [tolerance=±5% resistance=1k package=THT]
  R3 = Resistor [tolerance=±5% resistance=1k package=THT]
  R4 = Resistor [tolerance=±5% resistance=330 package=THT]
  R6 = Resistor [tolerance=±5% resistance=470 package="2512 [SMD]"]
  R7 = Resistor [tolerance=±5% resistance=680 package=THT]

nets:
  N1: Part1.A0, R3.Pin_1, R4.Pin_1
  N2: Part1.A1, R2.Pin_1, R7.Pin_1
  N3: Part1.A2, R1.Pin_1, R6.Pin_1
  N4: Part1.GND, R1.Pin_0, R2.Pin_0, R3.Pin_0, R4.Pin_0, R6.Pin_0, R7.Pin_0

notes:
  ARANO-VERTULFO
  MIDTERM PROJECT
  WYE-DELTA TRANSFORMATION USING ARDUINO MEGA 2560 (REV3)
  3 1000 OHMS RESISTORS
  1 330 OHMS RESISTOR
  1 470 OHMS RESISTOR
  1 680 OHMS RESISTOR
